# Fritzing sketch breadboardschematic (saved by Fritzing 0.8.7b)
breadboards: 1

parts:
  DS1 = DS18B20 1-Wire Temperature Sensor [part_number=DS18B20]
  R1 = Resistor [tolerance=±5% resistance=10k package=THT]
  R2 = Resistor [tolerance=±5% resistance=10k package=THT]
  C1 = Electrolytic Capacitor [capacitance=1µF package="100 mil [THT, electrolytic]"]
  C2 = Electrolytic Capacitor [capacitance=1µF package="100 mil [THT, electrolytic]"]
  R3 = Trimmer Potentiometer [maximum_resistance=10kΩ package=THT]
  S1 = Pushbutton [package="[THT]"]
  R4 = Resistor [tolerance=±5% resistance=15 package=THT]
  R5 = Resistor [tolerance=±5% resistance=15 package=THT]
  R6 = Resistor [tolerance=±5% resistance=10k package=THT]
  R7 = Resistor [tolerance=±10% resistance=10k package=THT]
  R8 = Resistor [tolerance=±5% resistance=47k package=THT]
  Part1 = Arduino Ethernet Shield (Rev3)
  LCD1 = LCD screen
  R9 = Resistor [tolerance=±5% resistance=10k package=THT]

nets:
  GND: DS1.GND, R1.Pin_1, R3.leg1, S1.Pin_1, S1.Pin_2, R6.Pin_1, Part1.D8, Part1.GND, LCD1.VSS, LCD1.R/W
  5V: DS1.DQ, R2.Pin_1, C1.-, C2.-, R3.leg2, R7.Pin_1, R8.Pin_1, Part1.5V, LCD1.VDD, LCD1.DB6, R9.Pin_0
  N1: DS1.VDD, R8.Pin_0, Part1.D7
  N2: R1.Pin_0, R2.Pin_0, C2.+, R4.Pin_0
  N3: C1.+, R5.Pin_0, R6.Pin_0, R7.Pin_0
  N4: R3.wiper, LCD1.V0
  N5: S1.Pin_3, S1.Pin_4, R9.Pin_1
  N6: R4.Pin_1, Part1.A0
  N7: R5.Pin_1, Part1.A1
  N8: Part1.A2, LCD1.DB5
  N9: Part1.A3, LCD1.DB4
  N10: Part1.A4/SDA, LCD1.E
  N11: Part1.A5/SCL, LCD1.RS
  N12: Part1.D2, LCD1.DB2
  N13: Part1.PWM_D3, LCD1.DB7
  N14: Part1.PWM_D5, LCD1.LED-
  N15: Part1.PWM_D6, LCD1.DB3
