# Fritzing sketch pcbnew (saved by Fritzing 0.8.7b)
circuit board: 17.2384cm x 11.8193cm
breadboards: 1

parts:
  R1 = Resistor [tolerance=±5% resistance=10k package=THT]
  R2 = Resistor [tolerance=±5% resistance=10k package=THT]
  R3 = Resistor [tolerance=±5% resistance=10k package=THT]
  R4 = Resistor [tolerance=±5% resistance=10k package=THT]
  C1 = Electrolytic Capacitor [capacitance=10µF voltage=16V package="100 mil [THT, electrolytic]"]
  C2 = Electrolytic Capacitor [capacitance=10µF voltage=16V package="100 mil [THT, electrolytic]"]
  S1 = Pushbutton [package="[THT]"]
  Componente1 = Arduino Ethernet Shield (Rev3)
  U1 = 2.5mm Audio Jack [package=stereojack2.5mm_specia_pogopins]
  U2 = 2.5mm Audio Jack [package=stereojack2.5mm_specia_pogopins]
  BURDEN4 = Resistor [tolerance=±5% resistance=13 package=THT]
  BURDEN5 = Resistor [tolerance=±5% resistance=13 package=THT]
  R6 = Resistor [tolerance=±5% resistance=10k package=THT]
  U4 = LCD-16X2 [package=lcd-16x2]
  S2 = Tilt Switch [package=THT]
  Componente2 = Arduino Ethernet Shield (Rev3)
  U5 = mystery part, 3 pins [chip_label=?]
  JP1 = Header 3 [package=screwterminal-3.5mm-3_lock.007s]
  R7 = Resistor [tolerance=±5% resistance=47k package=THT]

nets:
  N1: R1.Pin_0, R3.Pin_0, Componente1.5V, R6.Pin_1, JP1.3, R7.Pin_0
  N2: R1.Pin_1, R2.Pin_0, C1.+, U1.SLEEVE, BURDEN4.Pin_1
  N3: R2.Pin_1, R4.Pin_1, C1.-, C2.-, S1.Pin_3, S1.Pin_4, Componente1.D8, Componente1.GND, JP1.2
  N4: R3.Pin_1, R4.Pin_0, C2.+, U2.SLEEVE, BURDEN5.Pin_1
  N5: S1.Pin_1, R6.Pin_0
  N6: Componente1.A0, U2.LEFT, BURDEN5.Pin_0
  N7: Componente1.A1, U1.LEFT, BURDEN4.Pin_0
  N8: Componente1.D7, JP1.1, R7.Pin_1
  VSS: U4.VSS, U4.R_W, Componente2.GND, U5.pin3
  VDD: U4.VDD, U4.A, Componente2.5V, U5.pin1
  N9: U4.VO, U5.pin2
  N10: U4.RS, Componente2.A5/SCL
  N11: U4.E, Componente2.A4/SDA
  N12: U4.DB4, Componente2.D2
  N13: U4.DB5, Componente2.PWM_D6
  N14: U4.DB6, Componente2.A3
  N15: U4.DB7, Componente2.A2
  N16: U4.K, Componente2.PWM_D3
  N17: S2.Pin_1, Componente2.PWM_D5
